// Logisim project Commonbus-Mux.circ as structural Verilog: 1 circuit, main circuit main
module main (
  input  [2:0] in_1,
  input  in_2,
  input  in_3,
  input  [7:0] in_4,
  input  [7:0] in_5,
  input  [7:0] in_6,
  input  [7:0] in_7,
  input  [7:0] in_8,
  input  [7:0] in_9,
  input  [7:0] in_10,
  input  [7:0] in_11,
  output [7:0] out_12
);

  wire clock_1_out, multiplexer_2_out, multiplexer_3_out, multiplexer_4_out, multiplexer_5_out,
       multiplexer_6_out, multiplexer_7_out, multiplexer_8_out;
  wire [7:0] register_1_q, register_2_q, register_3_q, register_4_q, register_5_q, register_6_q,
       register_7_q, register_8_q;

  Multiplexer #(.select(3), .width(8)) multiplexer_1 (
    .in0(register_1_q), .in1(register_2_q), .in2(register_3_q), .in3(register_4_q), .in4(register_5_q),
    .in5(register_6_q), .in6(register_7_q), .in7(register_8_q), .out(out_12), .sel(in_1), .en(in_2));
  Register register_1 (.D(in_4), .en(in_3), .Q(register_1_q), .clk(clock_1_out));  // open: clr
  Clock clock_1 (.out(clock_1_out));
  Multiplexer #(.select(3)) multiplexer_2 (.out(multiplexer_2_out));  // open: in0, in1, in2, in3, in4, in5, in6, in7, sel, en
  Register register_2 (.D(in_5), .en(in_3), .Q(register_2_q), .clk(clock_1_out));  // open: clr
  Multiplexer #(.select(3)) multiplexer_3 (.out(multiplexer_3_out));  // open: in0, in1, in2, in3, in4, in5, in6, in7, sel, en
  Register register_3 (.D(in_6), .en(in_3), .Q(register_3_q), .clk(clock_1_out));  // open: clr
  Multiplexer #(.select(3)) multiplexer_4 (.out(multiplexer_4_out));  // open: in0, in1, in2, in3, in4, in5, in6, in7, sel, en
  Register register_4 (.D(in_7), .en(in_3), .Q(register_4_q), .clk(clock_1_out));  // open: clr
  Multiplexer #(.select(3)) multiplexer_5 (.out(multiplexer_5_out));  // open: in0, in1, in2, in3, in4, in5, in6, in7, sel, en
  Register register_5 (.D(in_8), .Q(register_5_q), .clk(clock_1_out));  // open: en, clr
  Multiplexer #(.select(3)) multiplexer_6 (.out(multiplexer_6_out));  // open: in0, in1, in2, in3, in4, in5, in6, in7, sel, en
  Register register_6 (.D(in_9), .en(in_3), .Q(register_6_q), .clk(clock_1_out));  // open: clr
  Multiplexer #(.select(3)) multiplexer_7 (.out(multiplexer_7_out));  // open: in0, in1, in2, in3, in4, in5, in6, in7, sel, en
  Register register_7 (.D(in_10), .en(in_3), .Q(register_7_q), .clk(clock_1_out));  // open: clr
  Multiplexer #(.select(3)) multiplexer_8 (.out(multiplexer_8_out));  // open: in0, in1, in2, in3, in4, in5, in6, in7, sel, en
  Register register_8 (.D(in_11), .en(in_3), .Q(register_8_q), .clk(clock_1_out));  // open: clr
endmodule
