// Logisim project FullAdder.circ as structural Verilog: 1 circuit, main circuit main
module main (
  input  Input_A,
  input  Input_B,
  input  Input_C,
  input  Input_A_2,
  input  Input_B_2,
  output SUM,
  output CARRY,
  output SUM_2,
  output CARRY_2
);

  wire and_2_out, and_3_out, and_4_out;

  xor xor_1 (SUM_2, Input_B_2, Input_A_2);
  and and_1 (CARRY_2, Input_B_2, Input_A_2);
  ExactlyOne xor_2 (.out(SUM), .in0(Input_A), .in1(Input_B), .in2(Input_C));
  and and_2 (and_2_out, Input_C, Input_B);
  and and_3 (and_3_out, Input_A, Input_B);
  and and_4 (and_4_out, Input_C, Input_A);
  or or_1 (CARRY, and_2_out, and_3_out, and_4_out);

  // Notes on the sheet:
  //   HALF ADDER
  //   FULL ADDER
endmodule
