// Logisim project binaryincrementor.circ as structural Verilog: 1 circuit, main circuit main
module main (
  input  A1,
  input  Logic_1,
  input  A0,
  input  A3,
  input  A2,
  output S1,
  output S0,
  output S3,
  output S2,
  output C3
);

  wire and_1_out, and_2_out, and_3_out;

  xor xor_1 (S0, A0, Logic_1);
  and and_1 (and_1_out, A0, Logic_1);
  xor xor_2 (S2, A2, and_3_out);
  and and_2 (and_2_out, A2, and_3_out);
  xor xor_3 (S1, A1, and_1_out);
  and and_3 (and_3_out, A1, and_1_out);
  xor xor_4 (S3, A3, and_2_out);
  and and_4 (C3, A3, and_2_out);

  // Notes on the sheet:
  //   C0
  //   C2
  //   Binary Incrementor
  //   C1
endmodule
