// Logisim project controlunit.circ as structural Verilog: 1 circuit, main circuit main
module main (
  input  Enable,
  input  [2:0] in_2,
  input  in_3,
  input  Increment,
  input  Clear
);

  wire clock_1_out, d_ff_1_q, undriven;
  wire [3:0] counter_1_q;

  Clock clock_1 (.out(clock_1_out));
  D_Flip_Flop d_ff_1 (.clk(clock_1_out), .D(in_3), .Q(d_ff_1_q));  // open: Qn, preset, en, reset
  Counter #(.width(4), .max('hf)) counter_1 (
    .load(undriven), .count(Increment), .Q(counter_1_q), .clk(clock_1_out), .clr(Clear));  // open: D, carry
  Decoder #(.select(3)) decoder_1 (
    .out0(d_ff_1_q), .out1(d_ff_1_q), .out2(d_ff_1_q), .out3(d_ff_1_q), .out4(d_ff_1_q), .out5(d_ff_1_q),
    .out6(d_ff_1_q), .out7(d_ff_1_q), .sel(in_2), .en(Enable));
  Decoder #(.select(4)) decoder_2 (
    .out0(d_ff_1_q), .out1(d_ff_1_q), .out2(d_ff_1_q), .out3(d_ff_1_q), .out4(d_ff_1_q), .out5(d_ff_1_q),
    .out6(d_ff_1_q), .out7(d_ff_1_q), .out8(d_ff_1_q), .out9(d_ff_1_q), .out10(d_ff_1_q), .out11(d_ff_1_q),
    .out12(d_ff_1_q), .out13(d_ff_1_q), .out14(d_ff_1_q), .out15(d_ff_1_q), .sel(counter_1_q), .en(Enable));

  // Notes on the sheet:
  //   Clock
  //   I bit
  //   Sequence Counter
  //   3x8 Decoder
  //   4x16 Decoder
  //   Control Unit of Basic Computer
  //   Conventitional 
  //   Logic
  //   Gates
  //   Other Inputs
  //   Control Output
endmodule
