// Logisim project Shifter.circ as structural Verilog: 1 circuit, main circuit main
module main (
  input  [3:0] in_1,
  input  [3:0] in_2,
  input  [3:0] in_3,
  input  [3:0] in_4,
  input  [3:0] in_5,
  output [3:0] out_6,
  output [3:0] out_7,
  output [3:0] out_8,
  output [3:0] out_9,
  output [3:0] out_10
);

  Shifter #(.width(4)) shifter_1 (.in(in_1), .\dist (2'b01), .out(out_6));
  Shifter #(.width(4), .shift("lr")) shifter_2 (.in(in_3), .\dist (2'b01), .out(out_8));
  Shifter #(.width(4), .shift("rl")) shifter_3 (.in(in_5), .\dist (2'b01), .out(out_10));
  Shifter #(.width(4), .shift("rr")) shifter_4 (.in(in_2), .\dist (2'b01), .out(out_7));
  Shifter #(.width(4), .shift("ar")) shifter_5 (.in(in_4), .\dist (2'b01), .out(out_9));

  // Notes on the sheet:
  //   Logical Left
  //   Logical Right
  //   Circular Left
  //   Arithmetic Right
  //   Circular Right
endmodule
