// Logisim project bininc.circ as structural Verilog: 1 circuit, main circuit main
module main (
  input  Logic_1,
  input  A0,
  input  A1,
  input  A2,
  input  A3,
  output S0,
  output S1,
  output S2,
  output S3,
  output C3
);

  wire adder_1_cout, adder_2_cout, adder_3_cout;

  Adder #(.width(1)) adder_1 (.a(Logic_1), .b(A0), .out(S0), .cout(adder_1_cout));  // open: cin
  Adder #(.width(1)) adder_2 (.a(adder_1_cout), .b(A1), .out(S1), .cout(adder_2_cout));  // open: cin
  Adder #(.width(1)) adder_3 (.a(adder_2_cout), .b(A2), .out(S2), .cout(adder_3_cout));  // open: cin
  Adder #(.width(1)) adder_4 (.a(adder_3_cout), .b(A3), .out(S3), .cout(C3));  // open: cin

  // Notes on the sheet:
  //   C0
  //   C1
  //   C2
  //   Binary Adder
endmodule
