// Logisim project mux data bus.circ as structural Verilog: 1 circuit, main circuit main
module main (
  input  in_1,
  input  in_2
);

  wire [1:1] undriven;
  wire [3:0] multiplexer_1_out, multiplexer_2_out, multiplexer_3_out, multiplexer_4_out;

  Multiplexer #(.select(2), .width(4)) multiplexer_1 (
    .out(multiplexer_1_out), .sel({undriven[1], in_2}), .en(in_1));  // open: in0, in1, in2, in3
  Register #(.width(4)) register_1 ();  // open: D, en, Q, clk, clr
  Multiplexer #(.select(2), .width(4)) multiplexer_2 (
    .out(multiplexer_2_out), .sel({undriven[1], in_2}), .en(in_1));  // open: in0, in1, in2, in3
  Register #(.width(4)) register_2 ();  // open: D, en, Q, clk, clr
  Multiplexer #(.select(2), .width(4)) multiplexer_3 (
    .out(multiplexer_3_out), .sel({undriven[1], in_2}), .en(in_1));  // open: in0, in1, in2, in3
  Register #(.width(4)) register_3 ();  // open: D, en, Q, clk, clr
  Multiplexer #(.select(2), .width(4)) multiplexer_4 (
    .out(multiplexer_4_out), .sel({undriven[1], in_2}), .en(in_1));  // open: in0, in1, in2, in3
  Register #(.width(4)) register_4 ();  // open: D, en, Q, clk, clr
  // Pins of 1 and 2 bits meet at {undriven[1], in_2}
endmodule
