// Logisim project practical2.circ as structural Verilog: 1 circuit, main circuit main
module main (
  input  x,
  input  y,
  output Z
);

  wire clock_1_out, d_ff_1_q, Da_out, Db_out, not_1_out, x_prime_B_out, x_prime_y_out, xA_out;

  not not_1 (not_1_out, x);
  Clock clock_1 (.out(clock_1_out));
  and x_prime_y (x_prime_y_out, not_1_out, y);
  and xA (xA_out, x, d_ff_1_q);
  or Da (Da_out, x_prime_y_out, xA_out);
  D_Flip_Flop d_ff_1 (.clk(clock_1_out), .D(Da_out), .Q(d_ff_1_q));  // open: Qn, preset, en, reset
  D_Flip_Flop d_ff_2 (.clk(d_ff_1_q), .D(Db_out), .Q(Z));  // open: Qn, preset, en, reset
  and x_prime_B (x_prime_B_out, not_1_out, Z);
  or Db (Db_out, x_prime_B_out, xA_out);

  // Notes on the sheet:
  //   Clock
  //   Filpflop A
  //   Flipflop B
endmodule
